# Fritzing sketch Pi_Schematic (saved by Fritzing 0.9.3b)
breadboards: 1

parts:
  Raspberry_Pi_1 = Raspberry Pi 3 [part_number=RPI-3-V1.2]
  LED1 = LED - 3mm [color="Blue (430nm)" package="3 mm [THT]"]
  U3 = HALL-EFFECT [package=sc70]
  R1 = Resistor [tolerance=±5% resistance=10k package=THT]
  U1 = ID-12_20 [package=id-12]
  LED3 = LED - 3mm [color="Green (570nm)" package="3 mm [THT]"]
  R2 = Resistor [tolerance=±5% resistance=10k package=THT]
  S1 = Momentary Switch [package=ksa_sealed_tac_switch]
  R3 = Resistor [tolerance=±5% resistance=10k package=THT]

nets:
  GND: Raspberry_Pi_1.GND, LED1.anode, U3.GND, U1.GNDT, U1.+_-, LED3.cathode, R3.Pin_0
  N1: Raspberry_Pi_1.GPIO27, LED1.cathode, U1.FUTURE
  N2: Raspberry_Pi_1.GPIO25, U3.OUT, R1.Pin_0, R2.Pin_1
  N3: Raspberry_Pi_1.GPIO15, U1.D0
  5V: Raspberry_Pi_1.5V, U3.VCC, R1.Pin_1, U1.5V
  N4: LED3.anode, R2.Pin_0
  N5: S1.1, R3.Pin_1
